# Fritzing sketch gpio_buttons (saved by Fritzing 0.7.11b)
breadboards: 1

parts:
  S1 = Pushbutton [package="[THT]"]
  S2 = Pushbutton [package="[THT]"]
  S3 = Pushbutton [package="[THT]"]
  S4 = Pushbutton [package="[THT]"]
  R1 = Resistor [tolerance=±5% resistance=1.5k package=THT]
  R2 = Resistor [tolerance=±5% resistance=1.5k package=THT]
  R3 = Resistor [tolerance=±5% resistance=1.5k package=THT]
  R4 = Resistor [tolerance=±5% resistance=1.5k package=THT]
  J1 = male pin header, 6 pins [form="♂ (male)"]

nets:
  GND: S1.Pin_1, S1.Pin_2, S2.Pin_1, S2.Pin_2, S3.Pin_1, S3.Pin_2, S4.Pin_1, S4.Pin_2, J1.pin1
  N1: S1.Pin_3, S1.Pin_4, R1.Pin_1, J1.pin5
  N2: S2.Pin_3, S2.Pin_4, R2.Pin_1, J1.pin4
  N3: S3.Pin_3, S3.Pin_4, R3.Pin_1, J1.pin3
  N4: S4.Pin_3, S4.Pin_4, R4.Pin_1, J1.pin2
  +3.3V: R1.Pin_0, R2.Pin_0, R3.Pin_0, R4.Pin_0, J1.pin6

notes:
  PiStation, GPIO Input Buttons, A
