# Fritzing sketch power_board (saved by Fritzing 0.7.11b)
stripboards: 1

parts:
  U1 = Voltage Regulator - 5V [package="TO220 [THT]"]
  C1 = Electrolytic Capacitor [capacitance=10µF voltage=16V package="100 mil [THT, electrolytic]"]
  C2 = Electrolytic Capacitor [capacitance=1µF package="100 mil [THT, electrolytic]"]
  J1 = male pin header, 2 pins [form="♂ (male)"]
  J3 = male pin header, 4 pins [form="♂ (male)"]
  J4 = male pin header, 2 pins [form="♂ (male)"]
  J5 = male pin header, 2 pins [form="♂ (male)"]
  J6 = male pin header, 2 pins [form="♂ (male)"]
  D1 = Rectifier Diode [part_number=1N4001 package="300 mil [THT]"]
  R1 = Resistor [tolerance=±5% resistance=22 package=THT]
  R2 = Resistor [tolerance=±5% resistance=22 power=5W package=THT]

nets:
  N1: U1.input_voltage, C1.+, R1.Pin_1, R2.Pin_1
  GND: U1.GND, C1.-, C2.-, J1.pin1, J3.pin2, J4.pin1, J5.pin1, J6.pin1
  N2: U1.output_voltage, C2.+, J6.pin2
  N3: J1.pin2, D1.anode
  +12V: J3.pin1, D1.cathode, R1.Pin_0, R2.Pin_0
  AUDIO: J3.pin3, J4.pin2
  VIDEO: J3.pin4, J5.pin2

notes:
  PiStation, Power and Signal Distribution, A
  Pi Audio Output
  Pi Video Output
  Pi Power Input
